# Fritzing sketch 02 (saved by Fritzing 0.9.3b)
breadboards: 1

parts:
  부품1 = Arduino Uno (Rev3)
  R1 = Rotary Potentiometer (Small) [maximum_resistance=100kΩ package=THT]
  J1 = Basic Servo

nets:
  N1: 부품1.A0, R1.wiper
  N2: 부품1.D9_PWM, J1.pulse
  GND: 부품1.GND, R1.leg1, J1.gnd
  5V: 부품1.5V, R1.leg2, J1.vcc
