# Fritzing sketch 03 (saved by Fritzing 0.9.3b)
breadboards: 1

parts:
  R1 = Resistor [tolerance=±5% resistance=10k package=THT]
  J1 = Basic Servo
  R2 = PHOTOCELL [package=photocell]
  부품1 = Arduino Uno (Rev3)

nets:
  GND: R1.Pin_0, J1.gnd, 부품1.GND
  N1: R1.Pin_1, R2.P$1, 부품1.A0
  VCC: J1.vcc, R2.P$2, 부품1.5V
  N2: J1.pulse, 부품1.D9_PWM
