# Fritzing sketch 04 (saved by Fritzing 0.9.3b)
breadboards: 1

parts:
  Ardunio_UNO = Arduino Uno (Rev3)
  J1 = Basic Servo
  S1 = Pushbutton [package="[THT]"]
  S2 = Pushbutton [package="[THT]"]
  R1 = Resistor [tolerance=±5% resistance=10k package=THT]
  R2 = Resistor [tolerance=±5% resistance=10k package=THT]

nets:
  N1: Ardunio_UNO.D9_PWM, J1.pulse
  N2: Ardunio_UNO.D12/MISO, S2.Pin_1, S2.Pin_2, R2.Pin_1
  N3: Ardunio_UNO.D13/SCK, R1.Pin_1
  5V: Ardunio_UNO.5V, J1.vcc, S1.Pin_4, S2.Pin_3, S2.Pin_4
  GND: Ardunio_UNO.GND, J1.gnd, R2.Pin_0
